// Logisim project CPU.circ as structural Verilog: 8 circuits, main circuit main
module main (
);

  wire ALUSrc, and_2_out, Branch, CLK, clock_1_out, comparator_1_eq, JR, Jump, Lbu, Link, Lui, MemRead,
       MemtoReg, MemWrite, RegDst, RegWrite, RST, Zero;
  wire [1:0] ALUOp;
  wire [2:0] Operation;
  wire [4:0] multiplexer_1_out, WriteReg;
  wire [25:0] ADDRESS;
  wire [31:0] AddrMod, ALU_Result, ALUA, ALUB, divider_1_out, divider_2_out, INMMEDIATExtended,
       multiplexer_2_out, multiplexer_4_out, multiplexer_7_out, multiplexer_8_out, multiplexer_9_out, PC4,
       PC_In, PC_Out, PCbeq, ReadData, ReadData2, shifter_1_out, UnsignedByte, UpperI, WriteData;
  wire [31:26] Instruction;

  Clock clock_1 (.out(clock_1_out));
  Comparator #(.width(32)) comparator_1 (
    .a({32{1'b0}}), .b({Instruction, ADDRESS}), .eq(comparator_1_eq));  // open: gt, lt
  Register #(.width(32)) PC (.D(PC_In), .Q(PC_Out), .clk(CLK), .clr(RST));  // open: en
  Divider #(.width(32)) divider_1 (.a(PC_Out), .b(32'h4), .out(divider_1_out));  // open: upper, rem
  and and_1 (CLK, clock_1_out, ~comparator_1_eq);  // AND_Gate
  ROM #(.addrWidth(24), .dataWidth(32)) InstructionMemory (.addr(divider_1_out[23:0]), .data({Instruction, ADDRESS}));
  Adder #(.width(32)) adder_1 (.a(PC_Out), .b(32'h4), .out(PC4));  // open: cin, cout
  assign INMMEDIATExtended = {{16{ADDRESS[15]}}, ADDRESS[15:0]};  // Bit_Extender bit_extender_1
  Button button_1 (.out(RST));
  Shifter #(.width(32)) shifter_1 (.in(INMMEDIATExtended), .\dist (5'b00010), .out(shifter_1_out));
  Adder #(.width(32)) adder_2 (.a(shifter_1_out), .b(PC4), .out(PCbeq));  // open: cin, cout
  Control control_1 (
    .OP(Instruction), .RegDst(RegDst), .MemRead(MemRead), .MemtoReg(MemtoReg), .MemWrite(MemWrite),
    .ALUOP(ALUOp), .ALUSrc(ALUSrc), .RegWrite(RegWrite), .Jump(Jump), .Branch(Branch), .Link(Link),
    .Lbu(Lbu), .Lui(Lui));
  JR_Control jr_control_1 (.FUNCT(ADDRESS[5:0]), .ALUOP(ALUOp), .JR(JR));
  Reg32 reg32_1 (
    .RegWrite(RegWrite), .WriteReg(WriteReg), .WriteData(WriteData), .ReadReg1(ADDRESS[25:21]),
    .ReadReg2(ADDRESS[20:16]), .Reset(RST), .ReadData1(ALUA), .ReadData2(ReadData2));
  ALUControl alucontrol_1 (.ALUOp(ALUOp), .funct(ADDRESS[5:0]), .ALU_operation(Operation));
  ALU alu_1 (.A(ALUA), .B(ALUB), .ALU_OP(Operation), .ALU_Result(ALU_Result), .Zero(Zero));
  lbu_alu lbu_alu_1 (.Word(ReadData), .AddrMod(AddrMod), .UnsignedByte(UnsignedByte));
  lui_alu lui_alu_1 (.inmmediate(ADDRESS[15:0]), .UpperInmediate(UpperI));
  and and_2 (and_2_out, Branch, Zero);
  Multiplexer #(.width(5)) multiplexer_1 (
    .in0(ADDRESS[20:16]), .in1(ADDRESS[15:11]), .out(multiplexer_1_out), .sel(RegDst));
  Multiplexer #(.width(32)) multiplexer_2 (.in0(PC4), .in1(PCbeq), .out(multiplexer_2_out), .sel(and_2_out));
  Divider #(.width(32)) divider_2 (.a(ALU_Result), .b(32'h4), .out(divider_2_out), .rem(AddrMod));  // open: upper
  RAM #(.addrWidth(24), .asyncread("true"), .clearpin("true"), .dataWidth(32)) ram_1 (
    .addr(divider_2_out[23:0]), .we(MemWrite), .oe(MemRead), .clk(CLK), .din(ReadData2), .dout(ReadData));  // open: clr
  Multiplexer #(.width(5)) multiplexer_3 (.in0(multiplexer_1_out), .in1({5{1'b1}}), .out(WriteReg), .sel(Link));
  Multiplexer #(.width(32)) multiplexer_4 (
    .in0(multiplexer_2_out), .in1({PC4[31:28], ADDRESS, 2'b00}), .out(multiplexer_4_out), .sel(Jump));
  Multiplexer #(.width(32)) multiplexer_5 (.in0(ReadData2), .in1(INMMEDIATExtended), .out(ALUB), .sel(ALUSrc));
  Multiplexer #(.width(32)) multiplexer_6 (.in0(multiplexer_4_out), .in1(ALUA), .out(PC_In), .sel(JR));
  Multiplexer #(.width(32)) multiplexer_7 (.in0(ALU_Result), .in1(ReadData), .out(multiplexer_7_out), .sel(MemtoReg));
  Multiplexer #(.width(32)) multiplexer_8 (.in0(multiplexer_7_out), .in1(PC4), .out(multiplexer_8_out), .sel(Link));
  Multiplexer #(.width(32)) multiplexer_9 (
    .in0(multiplexer_8_out), .in1(UnsignedByte), .out(multiplexer_9_out), .sel(Lbu));
  Multiplexer #(.width(32)) multiplexer_10 (.in0(multiplexer_9_out), .in1(UpperI), .out(WriteData), .sel(Lui));

  // Other names for the same wires on the sheet: FUNCT[5:0] = ADDRESS[5:0]; INMMEDIATE[15:0] = ADDRESS[15:0];
  //   Instruction[25:0] = ADDRESS; PCJump[31:2] = {PC4[31:28], ADDRESS}; SHAMT[4:0] = ADDRESS[10:6];
  //   RD[4:0] = ADDRESS[15:11]; ReadReg2[4:0] = ADDRESS[20:16]; RT[4:0] = ADDRESS[20:16];
  //   ReadReg1[4:0] = ADDRESS[25:21]; RS[4:0] = ADDRESS[25:21]; OP[5:0] = Instruction; ReadData1[31:0] = ALUA

  // Notes on the sheet:
  //   R Type Instructions
  //   contents of InstructionMemory (hex, n*v repeats v):
  //   3c1d0001 3c100000 c00001e 408820 609020 c000026 409820 c00002e 40a820 60a020 8fa20000 8fa30004
  //   3b2e820 3b2e820 40b820 60b020 2e02020 2c02820 2a03020 2803820 c000052 408820 608020 8fa20000
  //   8fa30004 3b2e820 3b2e820 409820 609020 8000072 3c080001 3c090002 109402a 1084820 1294820 1001020
  //   1201820 3e00008 2524020 1084020 1084820 1294020 1094020 1124020 1001020 3e00008 3c19ffff 3c18ffff
  //   3c0f0001 3c0e0001 6020 2005820 3c0a0000 11930013 8d690000 11400007 309402a 11000001 120c020 12e402a
  //   11000001 1207020 8000045 329402a 11000001 120c820 12f402a 11000001 1207820 1405027 1725820 1916020
  //   8000035 3201020 3001820 3b2e822 3b2e822 afa20000 afa30004 1e01020 1c01820 3e00008 2004020 5020
  //   3c190000 3c180000 3c0f0000 3c0e0000 11530010 8d090000 11240001 800005d 331c820 11250001 8000060
  //   311c020 11260001 8000063 1f17820 11270001 8000066 1d17020 1124020 1515020 1000ffef 3201020 3001820
  //   3b2e822 3b2e822 afa20000 afa30004 1e01020 1c01820 3e00008
  //   I Type Instructions
  //   J Type Instructions
endmodule

module Reg32 (
  input  RegWrite,
  input  [4:0] WriteReg,
  input  [31:0] WriteData,
  input  [4:0] ReadReg1,
  input  [4:0] ReadReg2,
  input  Reset,
  output [31:0] ReadData1,
  output [31:0] ReadData2
);

  wire CLK, W0, W1, W2, W3, W4, W5, W6, W7, W8, W9, W10, W11, W12, W13, W14, W15, W16, W17, W18, W19, W20,
       W21, W22, W23, W24, W25, W26, W27, W28, W29, W30, W31;
  wire [31:0] R0, R1, R2, R3, R4, R5, R6, R7, R8, R9, R10, R11, R12, R13, R14, R15, R16, R17, R18, R19, R20,
       R21, R22, R23, R24, R25, R26, R27, R28, R29, R30, R31;

  Register #(.width(32)) register_1 (.D({32{1'b0}}), .en(W0), .clk(CLK), .Q(R0), .clr(Reset));
  Register #(.width(32)) register_2 (.D(WriteData), .en(W4), .clk(CLK), .Q(R4), .clr(Reset));
  Register #(.width(32)) register_3 (.D(WriteData), .en(W8), .clk(CLK), .Q(R8), .clr(Reset));
  Register #(.width(32)) register_4 (.D(WriteData), .en(W12), .clk(CLK), .Q(R12), .clr(Reset));
  Register #(.width(32)) register_5 (.D(WriteData), .en(W16), .clk(CLK), .Q(R16), .clr(Reset));
  Register #(.width(32)) register_6 (.D(WriteData), .en(W20), .clk(CLK), .Q(R20), .clr(Reset));
  Register #(.width(32)) register_7 (.D(WriteData), .en(W24), .clk(CLK), .Q(R24), .clr(Reset));
  Register #(.width(32)) register_8 (.D(WriteData), .en(W28), .clk(CLK), .Q(R28), .clr(Reset));
  Register #(.width(32)) register_9 (.D(WriteData), .en(W1), .clk(CLK), .Q(R1), .clr(Reset));
  Register #(.width(32)) register_10 (.D(WriteData), .en(W5), .clk(CLK), .Q(R5), .clr(Reset));
  Register #(.width(32)) register_11 (.D(WriteData), .en(W9), .clk(CLK), .Q(R9), .clr(Reset));
  Register #(.width(32)) register_12 (.D(WriteData), .en(W13), .clk(CLK), .Q(R13), .clr(Reset));
  Register #(.width(32)) register_13 (.D(WriteData), .en(W17), .clk(CLK), .Q(R17), .clr(Reset));
  Register #(.width(32)) register_14 (.D(WriteData), .en(W21), .clk(CLK), .Q(R21), .clr(Reset));
  Register #(.width(32)) register_15 (.D(WriteData), .en(W25), .clk(CLK), .Q(R25), .clr(Reset));
  Register #(.width(32)) register_16 (.D(WriteData), .en(W29), .clk(CLK), .Q(R29), .clr(Reset));
  Register #(.width(32)) register_17 (.D(WriteData), .en(W2), .clk(CLK), .Q(R2), .clr(Reset));
  Register #(.width(32)) register_18 (.D(WriteData), .en(W6), .clk(CLK), .Q(R6), .clr(Reset));
  Register #(.width(32)) register_19 (.D(WriteData), .en(W10), .clk(CLK), .Q(R10), .clr(Reset));
  Register #(.width(32)) register_20 (.D(WriteData), .en(W14), .clk(CLK), .Q(R14), .clr(Reset));
  Register #(.width(32)) register_21 (.D(WriteData), .en(W18), .clk(CLK), .Q(R18), .clr(Reset));
  Register #(.width(32)) register_22 (.D(WriteData), .en(W22), .clk(CLK), .Q(R22), .clr(Reset));
  Register #(.width(32)) register_23 (.D(WriteData), .en(W26), .clk(CLK), .Q(R26), .clr(Reset));
  Register #(.width(32)) register_24 (.D(WriteData), .en(W30), .clk(CLK), .Q(R30), .clr(Reset));
  Register #(.width(32)) register_25 (.D(WriteData), .en(W3), .clk(CLK), .Q(R3), .clr(Reset));
  Register #(.width(32)) register_26 (.D(WriteData), .en(W7), .clk(CLK), .Q(R7), .clr(Reset));
  Register #(.width(32)) register_27 (.D(WriteData), .en(W11), .clk(CLK), .Q(R11), .clr(Reset));
  Register #(.width(32)) register_28 (.D(WriteData), .en(W15), .clk(CLK), .Q(R15), .clr(Reset));
  Register #(.width(32)) register_29 (.D(WriteData), .en(W19), .clk(CLK), .Q(R19), .clr(Reset));
  Register #(.width(32)) register_30 (.D(WriteData), .en(W23), .clk(CLK), .Q(R23), .clr(Reset));
  Register #(.width(32)) register_31 (.D(WriteData), .en(W27), .clk(CLK), .Q(R27), .clr(Reset));
  Register #(.width(32)) register_32 (.D(WriteData), .en(W31), .clk(CLK), .Q(R31), .clr(Reset));
  Clock clock_1 (.out(CLK));
  Multiplexer #(.select(5), .width(32)) multiplexer_1 (
    .in0(R0), .in1(R1), .in2(R2), .in3(R3), .in4(R4), .in5(R5), .in6(R6), .in7(R7), .in8(R8), .in9(R9),
    .in10(R10), .in11(R11), .in12(R12), .in13(R13), .in14(R14), .in15(R15), .in16(R16), .in17(R17),
    .in18(R18), .in19(R19), .in20(R20), .in21(R21), .in22(R22), .in23(R23), .in24(R24), .in25(R25),
    .in26(R26), .in27(R27), .in28(R28), .in29(R29), .in30(R30), .in31(R31), .out(ReadData1), .sel(ReadReg1));
  Multiplexer #(.select(5), .width(32)) multiplexer_2 (
    .in0(R0), .in1(R1), .in2(R2), .in3(R3), .in4(R4), .in5(R5), .in6(R6), .in7(R7), .in8(R8), .in9(R9),
    .in10(R10), .in11(R11), .in12(R12), .in13(R13), .in14(R14), .in15(R15), .in16(R16), .in17(R17),
    .in18(R18), .in19(R19), .in20(R20), .in21(R21), .in22(R22), .in23(R23), .in24(R24), .in25(R25),
    .in26(R26), .in27(R27), .in28(R28), .in29(R29), .in30(R30), .in31(R31), .out(ReadData2), .sel(ReadReg2));
  Decoder #(.select(5)) decoder_1 (
    .out0(W0), .out1(W1), .out2(W2), .out3(W3), .out4(W4), .out5(W5), .out6(W6), .out7(W7), .out8(W8),
    .out9(W9), .out10(W10), .out11(W11), .out12(W12), .out13(W13), .out14(W14), .out15(W15), .out16(W16),
    .out17(W17), .out18(W18), .out19(W19), .out20(W20), .out21(W21), .out22(W22), .out23(W23), .out24(W24),
    .out25(W25), .out26(W26), .out27(W27), .out28(W28), .out29(W29), .out30(W30), .out31(W31),
    .sel(WriteReg), .en(RegWrite));

  // Other names for the same wires on the sheet: R = Reset; WD[31:0] = WriteData
endmodule

module ALU (
  input  [31:0] A,
  input  [31:0] B,
  input  [2:0] ALU_OP,
  output [31:0] ALU_Result,
  output Zero
);

  wire [0:0] SLT;
  wire [31:0] ADD, LAND, LNOR, LOR, SUB;

  Adder #(.width(32)) adder_1 (.a(A), .b(B), .out(ADD));  // open: cin, cout
  Subtractor #(.width(32)) subtractor_1 (.a(A), .b(B), .out(SUB));  // open: bin, bout
  assign LAND = A & B;  // AND_Gate and_1, 32 bits wide
  assign LOR = A | B;  // OR_Gate or_1, 32 bits wide
  assign LNOR = ~LOR;  // NOT_Gate not_1, 32 bits wide
  Comparator #(.width(32)) comparator_1 (.a(A), .b(B), .lt(SLT[0]));  // open: gt, eq
  Multiplexer #(.select(3), .width(32)) multiplexer_1 (
    .in0(LAND), .in1(LOR), .in2(ADD), .in4(LNOR), .in6(SUB), .in7({{31{1'b0}}, SLT[0]}), .out(ALU_Result),
    .sel(ALU_OP));  // open: in3, in5
  Comparator #(.width(32)) comparator_2 (.a({32{1'b0}}), .b(ALU_Result), .eq(Zero));  // open: gt, lt
endmodule

module Control (
  input  [5:0] OP,
  output RegDst,
  output MemRead,
  output MemtoReg,
  output MemWrite,
  output [1:0] ALUOP,
  output ALUSrc,
  output RegWrite,
  output Jump,
  output Branch,
  output Link,
  output Lbu,
  output Lui
);

  wire and_6_out, and_7_out, and_8_out, and_9_out, and_10_out, and_11_out, not_1_out, not_2_out, not_3_out,
       not_4_out, not_5_out;

  not not_1 (not_1_out, OP[5]);
  not not_2 (not_2_out, OP[3]);
  not not_3 (not_3_out, OP[2]);
  not not_4 (not_4_out, OP[1]);
  not not_5 (not_5_out, OP[0]);
  and and_1 (RegDst, not_1_out, not_2_out);
  and and_2 (MemRead, OP[5], not_2_out);
  and and_3 (MemWrite, OP[3], not_3_out);
  and and_4 (ALUOP[1], not_1_out, not_3_out);
  and and_5 (ALUOP[0], not_1_out, OP[2]);
  or or_1 (ALUSrc, OP[0], OP[5]);
  and and_6 (and_6_out, not_3_out, not_4_out);
  and and_7 (and_7_out, not_2_out, OP[0]);
  and and_8 (and_8_out, OP[2], OP[0]);
  and and_9 (and_9_out, OP[5], not_2_out);
  and and_10 (and_10_out, not_1_out, not_2_out, OP[1]);
  and and_11 (and_11_out, OP[1], not_5_out);
  and and_12 (Branch, not_1_out, OP[2], not_5_out);
  and and_13 (Link, not_1_out, not_2_out, OP[0]);
  and and_14 (Lbu, OP[5], OP[2]);
  and and_15 (Lui, not_1_out, OP[3]);
  or or_2 (RegWrite, and_6_out, and_7_out, and_8_out, and_9_out);
  or or_3 (Jump, and_10_out, and_11_out);

  assign MemtoReg = OP[0];
endmodule

module lbu_alu (
  input  [31:0] Word,
  input  [31:0] AddrMod,
  output [31:0] UnsignedByte
);

  wire [31:0] multiplier_1_out, shifter_1_out;

  Multiplier #(.width(32)) multiplier_1 (.a(AddrMod), .b(32'h8), .out(multiplier_1_out));  // open: cin, cout
  Shifter #(.shift("lr"), .width(32)) shifter_1 (.in(Word), .\dist (multiplier_1_out[4:0]), .out(shifter_1_out));
  assign UnsignedByte = shifter_1_out & 32'hff;  // AND_Gate and_1, 32 bits wide
endmodule

module lui_alu (
  input  [15:0] inmmediate,
  output [31:0] UpperInmediate
);


  assign UpperInmediate = {inmmediate, {16{1'b0}}};
endmodule

module ALUControl (
  input  [1:0] ALUOp,
  input  [5:0] funct,
  output [2:0] ALU_operation
);

  wire and_1_out, and_2_out, and_3_out, not_1_out, not_2_out, not_3_out;

  not not_1 (not_1_out, ALUOp[1]);
  not not_2 (not_2_out, funct[2]);
  not not_3 (not_3_out, funct[1]);
  and and_1 (and_1_out, ALUOp[1], funct[1]);
  or or_1 (ALU_operation[1], not_1_out, not_2_out);
  and and_2 (and_2_out, ALUOp[1], not_3_out, funct[0]);
  and and_3 (and_3_out, ALUOp[1], funct[5], funct[3]);
  or or_2 (ALU_operation[2], ALUOp[0], and_1_out);
  or or_3 (ALU_operation[0], and_2_out, and_3_out);
endmodule

module JR_Control (
  input  [5:0] FUNCT,
  input  [1:0] ALUOP,
  output JR
);

  wire and_1_out, and_2_out;

  and and_1 (and_1_out, ~FUNCT[0], ~FUNCT[1], ~FUNCT[2], FUNCT[3], ~FUNCT[4], ~FUNCT[5]);  // AND_Gate
  and and_2 (and_2_out, ~ALUOP[0], ALUOP[1]);  // AND_Gate
  and and_3 (JR, and_1_out, and_2_out);
endmodule
